# Fritzing sketch DIagrama_electrico_G5 (saved by Fritzing 0.9.6b)
breadboards: 1

parts:
  Mod1 = Raspberry Pi 4B
  Componente1 = RFID-RC522-v3

nets:
  5V: Mod1.5V, Componente1.3.3V
  GND: Mod1.GND, Componente1.GND
  N1: Mod1.GPIO10, Componente1.MOSI
  N2: Mod1.GPIO9, Componente1.MISO
  N3: Mod1.GPIO25, Componente1.RST
  N4: Mod1.GPIO11, Componente1.SCK
  N5: Mod1.GPIO8, Componente1.SDA

notes:
  SDA se conecta al Pin 24 .
  SCK se conecta al Pin 23 .
  MOSI se conecta al Pin 19 .
  MISO se conecta al Pin 21 .
  GND se conecta al Pin 6 .
  RST se conecta al Pin 22 .
  3.3v se conecta al Pin 1
  Raspberry PI 4 Model B
  RFID RC522

custom parts:
  RFID-RC522-v3: A simple China made RFID-RC522 Reader (6x4 cm); do check the pin labels, as this is a MFRC522 based clone.

// code stored in the sketch: Codigo.ino
#!/usr/bin/env python

import RPi.GPIO as GPIO
from mfrc522 import simpleMFRC522

obj = SimpleMFRC522()

try:
        leer = input('Nuevo Personal:')
        print("Ponga su tarjeta para registrarse")
        obj.write(leer)
        print("Tarjeta leida")
finally:
        GPIO.cleanup()
        
try: 
        id, leer= obj.read()
        print(id)
        print(leer)
finally:
        GPIO.cleanup()
